# Fritzing sketch mozvending (saved by Fritzing 1.0.1rc)
breadboards: 1

parts:
  Mod1 = Amica NodeMCU DEVKIT 1.0
  SM1 = 28BYJ-48 Stepper Motor [part_number=28BYJ-48]
  Driver1 = 28BYJ-48 Driver Module [part_number=ULN2003 package=THT]
  S1 = Round Pushbutton
  VCC1 = 4 x AAA Battery Mount

nets:
  N1: Mod1.pin1, Mod1.pin_10, Mod1.pin_26
  N2: Mod1.pin2, Mod1.pin_9, Mod1.pin_25, Mod1.pin_29, Driver1.GND, S1.leg1, VCC1.-
  N3: Mod1.pin6, S1.leg0
  N4: Mod1.pin7, Driver1.IN4
  N5: Mod1.pin8, Driver1.IN3
  N6: Mod1.pin_13, Driver1.IN2
  N7: Mod1.pin_14, Driver1.IN1
  N8: Mod1.pin_30, Driver1.Vmotor, VCC1.+
  N9: SM1.blue-pin, Driver1.blue-pin
  N10: SM1.pink-pin, Driver1.pink-pin
  N11: SM1.yellow-pin, Driver1.yellow-pin
  N12: SM1.orange-pin, Driver1.orange-pin
  N13: SM1.red-pin, Driver1.red-pin

notes:
  MozVending, NodeMCU 0.9 rotating a stepper motor on pushbutton press, 0.1

custom parts:
  28BYJ-48 Stepper Motor: Unipolar Stepper Motor 28BYJ-48 Top coil - pink & orange Bottom coil - blue & yellow Common rail - red Connector pins: blue - pink - yellow - orange - red
  28BYJ-48 Driver Module: ULN2003 Driver Module for the 28BYJ-48 Unipolar Stepper Motor LED A - Blue wire - Bottom coil left LED B - Pink wire - Top coil left LED C - Yellow wire - Bottom coil right LED D - Orange wire - Top coil right Common rail - red Connector pins: blue - pink - yellow - orange - red Control pins - IN1 to IN4 Power pins - GND & Vmotor (5-12V) On/Off jumper (if removed, power to motor is cut).
